# Fritzing sketch main_circuit (saved by Fritzing 0.8.7b)
circuit board: 8.46667cm x 5.64444cm
breadboards: 1

parts:
  R_RESET = Resistor [tolerance=±20% resistance=10k package=THT]
  C_CPU_POWER = Ceramic Capacitor [capacitance=100nF package="100 mil [THT, multilayer]"]
  U1 = atmega328 [package=dip]
  ISP = AVR 10pin ISP [form="♂ (shrouded male)" package=THT]
  RTC1 = Chronodot [chip_label=RTC package="DIP (Dual Inline) [THT]"]
  RESET_BUTTON = Pushbutton [package=THT]
  RTC_PROTECT = Rectifier Diode [part_number=1N4001 package="300 mil [THT]"]
  AUDIO1 = Adafruit 2.8W stereo amplifier with I2C [chip_label=AUDIO package="DIP (Dual Inline) [THT]"]
  SDCARD = microSD Socket [package="Molex 502774-0891 [SMD]"]
  D1 = SOLAR-IXYS [package=solarbit-12x1]
  BAT = DC Power [voltage=3.6V]
  DCF1 = DCF77 [chip_label=IC package="DIP (Dual Inline) [THT]"]
  DISPLAY = IC, DIP package, 4 pins [chip_label=LED]
  S_L = Pushbutton [package=THT]
  S_M = Pushbutton [package=THT]
  S_R = Pushbutton [package=THT]
  C3 = Electrolytic Capacitor [capacitance=4.7µF voltage=10V package="100 mil [THT, electrolytic]"]
  LIGHT = Pushbutton [package=THT]
  R_LIGHT = Resistor [tolerance=±5% resistance=10k package=THT]
  R_TIMER_INT = Resistor [tolerance=±5% resistance=10k package=THT]
  D2 = Diode [part_number=germanium package=diode-1n4001]
  U2 = SPDT Slide Switch [package=ayz0202]

nets:
  N1: R_RESET.Pin_0, C_CPU_POWER.1, U1.VCC, U1.AVCC, ISP.pin2, AUDIO1.pin1, AUDIO1.pin10, C3.+, R_LIGHT.Pin_0, R_TIMER_INT.Pin_0, U2.3
  N2: R_RESET.Pin_1, U1.RESET, ISP.pin5, RESET_BUTTON.leg1
  GND: C_CPU_POWER.0, U1.GND, ISP.pin4, ISP.pin6, ISP.pin8, ISP.pin10, RTC1.pin4, RESET_BUTTON.leg0, AUDIO1.pin2, AUDIO1.pin4, AUDIO1.pin7, SDCARD.GND, D1.A, BAT.V-, DCF1.pin2, DCF1.pin4, DISPLAY.pin2, S_L.leg1, S_M.leg1, S_R.leg1, C3.-, LIGHT.leg1
  N3: U1.D2, LIGHT.leg0, R_LIGHT.Pin_1
  N4: U1.D3_(PWM), RTC1.pin7, R_TIMER_INT.Pin_1
  N5: U1.D4, DISPLAY.pin1
  N6: U1.D5_(PWM), DCF1.pin1
  N7: U1.D6_(PWM), DCF1.pin3
  N8: U1.D7, SDCARD.VCC
  N9: U1.D8, AUDIO1.pin3
  N10: U1.D9_(PWM), AUDIO1.pin5
  N11: U1.D10_(PWM), SDCARD.CS
  N12: U1.D11_(PWM), ISP.pin1, SDCARD.DI
  N13: U1.D12, ISP.pin9, SDCARD.DO
  N14: U1.D13, ISP.pin7, SDCARD.SCK
  N15: U1.A0, RTC_PROTECT.anode
  N16: U1.A1, S_R.leg0
  N17: U1.A2, S_M.leg0
  N18: U1.A3, S_L.leg0
  N19: U1.A4, RTC1.pin1, AUDIO1.pin9, DISPLAY.pin3
  N20: U1.A5, RTC1.pin2, AUDIO1.pin8, DISPLAY.pin4
  N21: RTC1.pin3, RTC_PROTECT.cathode
  N22: D1.C, D2.A
  N23: BAT.V+, U2.6
  N24: D2.C, U2.2, U2.5

custom parts:
  atmega328: Atmel ATmega328 microcontroller.
  AVR 10pin ISP: Generic shrouded header
  Chronodot: A DIP stand-in part for whatever IC you want. With 8 pins on a 300mil dual inline package (DIP) footprint.
  Adafruit 2.8W stereo amplifier with I2C: A DIP stand-in part for whatever IC you want. With 10 pins on a 300mil dual inline package (DIP) footprint.
  DCF77: A DIP stand-in part for whatever IC you want. With 4 pins on a 300mil dual inline package (DIP) footprint.
